# Fritzing sketch Servo_Pan_and_tilt (saved by Fritzing 0.9.1b)
breadboards: 1

parts:
  Onderdeel1 = Arduino Uno (Rev3)
  VCC1 = Battery block 9V  # not connected
  VCC2 = Battery block 9V
  U3 = JOYSTICK-PSP1000 [package=joystick-psp1000]
  J1 = Basic Servo [part_number=Zaxis]
  J2 = Basic Servo

nets:
  N1: Onderdeel1.A2, U3.X
  N2: Onderdeel1.A4/SDA, U3.Y
  N3: Onderdeel1.D5_PWM, J1.pulse
  N4: Onderdeel1.D6_PWM, J2.pulse
  5V: Onderdeel1.5V, U3.VCC
  GND: Onderdeel1.GND, VCC2.-, U3.GND, J1.gnd, J2.gnd
  VCC: VCC2.+, J1.vcc, J2.vcc

// code stored in the sketch: joystick_pan_and_tilt.ino
/* joystick Controlled panning and tilting Servo 
simple code I wrote to control servos
using analog input like a joystick 
Two servo's one for each axis Z and X

made by Marcel C.
        mmc.mars@gmail.com  */

#include <Servo.h>

Servo servoZ;
Servo servoX;

const int joystickZ = A4;
const int joystickX = A2;

int sensorValueZ = 0;
int outputValueZ = 0;
int sensorValueX = 0;
int outputValueX = 0;
int turnZ = 0;
int turnX = 0;

void setup()
{
  Serial.begin(9600);
  servoZ.attach(5);
  servoX.attach(6);
}

void loop()
{
  {
    if (outputValueZ > 90)
    {
      servoZ.write(turnZ += 1);
    }
  }
  {
    if (outputValueZ > 10)
    {
      servoZ.write(turnZ += 2);
    }
  }
  {
    if (outputValueZ < 160)
    {
      servoZ.write(turnZ -= 1);
    }
  }
  {
    if (outputValueZ < 245)
    {
      servoZ.write(turnZ -= 2);
    }
  }   
  sensorValueZ = analogRead(joystickZ);            
  outputValueZ = map(sensorValueZ, 0, 1023, 0, 255); 
  Serial.print("sensorZ = " );                       
  Serial.print(sensorValueZ);      
  Serial.print("\t outputZ = ");      
  Serial.println(outputValueZ);  
  {
    if (outputValueX > 90)
    {
      servoX.write(turnX += 1);
    }
  }
  {
    if (outputValueX > 10)
    {
      servoX.write(turnX += 2);
    }
  }
  {
    if (outputValueX < 160)
    {
      servoX.write(turnX -= 1);
    }
  }
  {
    if (outputValueX < 245)
    {
      servoX.write(turnX -= 2);
    }
  }  
  sensorValueX = analogRead(joystickX);            
  outputValueX = map(sensorValueX, 0, 1023, 0, 255); 
  Serial.print("sensorX = " );                       
  Serial.print(sensorValueX);      
  Serial.print("\t outputX = ");      
  Serial.println(outputValueX);  
}
